// Logisim project E8BC.circ as structural Verilog
module ALU (
  input  [7:0] A,
  input  [2:0] FN,
  input  [7:0] B,
  input  [1:0] REG,
  input  WC,
  input  CF,
  output [7:0] OUT,
  output CY_OUT
);

  wire adder_1_cout, and_2_out, and_3_out, multiplexer_2_out, not_1_out, not_2_out, not_3_out,
       subtractor_1_bout;
  wire [7:0] adder_1_out, AND_out_3, divider_1_out, multiplexer_1_out, multiplier_1_out, OR_out_3,
       subtractor_1_out, XOR_out_3;

  Multiplexer #(.select(2), .width(8), .enable("false")) multiplexer_1 (
    .in0(B), .in1({8{1'b0}}), .in2(8'h1), .out(multiplexer_1_out), .sel(REG));  // open: in3
  AND8b AND (.in_1(A), .in_2(multiplexer_1_out), .out_3(AND_out_3));
  OR8b OR (.in_1(A), .in_2(multiplexer_1_out), .out_3(OR_out_3));
  XOR8b XOR (.in_1(A), .in_2(multiplexer_1_out), .out_3(XOR_out_3));
  Adder adder_1 (.a(A), .b(multiplexer_1_out), .out(adder_1_out), .cin(multiplexer_2_out), .cout(adder_1_cout));
  Subtractor subtractor_1 (
    .a(A), .b(multiplexer_1_out), .out(subtractor_1_out), .bin(multiplexer_2_out), .bout(subtractor_1_bout));
  Multiplexer #(.enable("false")) multiplexer_2 (.in0(1'b0), .in1(CF), .out(multiplexer_2_out), .sel(WC));
  Multiplier multiplier_1 (.a(A), .b(multiplexer_1_out), .out(multiplier_1_out));  // open: cin, cout
  Divider divider_1 (.a(A), .b(multiplexer_1_out), .out(divider_1_out));  // open: upper, rem
  assign CY_OUT = and_2_out ? adder_1_cout : 1'bz;  // Controlled_Buffer controlled_buffer_1
  assign CY_OUT = and_3_out ? subtractor_1_bout : 1'bz;  // Controlled_Buffer controlled_buffer_2
  Multiplexer #(.select(3), .width(8), .enable("false")) multiplexer_3 (
    .in1(AND_out_3), .in2(OR_out_3), .in3(XOR_out_3), .in4(adder_1_out), .in5(subtractor_1_out),
    .in6(multiplier_1_out), .in7(divider_1_out), .out(OUT), .sel(FN));  // open: in0
  not not_1 (not_1_out, FN[1]);
  not not_2 (not_2_out, FN[2]);
  not not_3 (not_3_out, FN[1]);
  and and_2 (and_2_out, FN[0], not_1_out, not_2_out);
  and and_3 (and_3_out, FN[0], not_3_out, FN[2]);

  // Notes on the sheet:
  //   CY_OUT: pull=up
  //   WC: pull=up
  //   CF: pull=up
  //   B: pull=up
  //   OUT: pull=up
  //   FN: pull=up
  //   A: pull=up
  //   REG: pull=up
  //   000 - nop
  //   FN
  //   001 - AND
  //   010 - OR
  //   011 - XOR
  //   100 - ADD
  //   101 - SUB
  //   110 - MUL
  //   111 - DIV
endmodule

module AND8b (
  input  [7:0] in_1,
  input  [7:0] in_2,
  output [7:0] out_3
);

  and and_1 (out_3[0], in_1[0], in_2[0]);
  and and_2 (out_3[1], in_1[1], in_2[1]);
  and and_3 (out_3[2], in_1[2], in_2[2]);
  and and_4 (out_3[3], in_1[3], in_2[3]);
  and and_5 (out_3[4], in_1[4], in_2[4]);
  and and_6 (out_3[5], in_1[5], in_2[5]);
  and and_7 (out_3[6], in_1[6], in_2[6]);
  and and_8 (out_3[7], in_1[7], in_2[7]);

  // Notes on the sheet:
  //   in_1: pull=up
  //   in_2: pull=up
  //   out_3: pull=up
endmodule

module OR8b (
  input  [7:0] in_1,
  input  [7:0] in_2,
  output [7:0] out_3
);

  or or_1 (out_3[0], in_1[0], in_2[0]);
  or or_2 (out_3[1], in_1[1], in_2[1]);
  or or_3 (out_3[2], in_1[2], in_2[2]);
  or or_4 (out_3[3], in_1[3], in_2[3]);
  or or_5 (out_3[4], in_1[4], in_2[4]);
  or or_6 (out_3[5], in_1[5], in_2[5]);
  or or_7 (out_3[6], in_1[6], in_2[6]);
  or or_8 (out_3[7], in_1[7], in_2[7]);

  // Notes on the sheet:
  //   in_2: pull=up
  //   in_1: pull=up
  //   out_3: pull=up
endmodule

module XOR8b (
  input  [7:0] in_1,
  input  [7:0] in_2,
  output [7:0] out_3
);

  xor xor_1 (out_3[0], in_1[0], in_2[0]);
  xor xor_2 (out_3[1], in_1[1], in_2[1]);
  xor xor_3 (out_3[2], in_1[2], in_2[2]);
  xor xor_4 (out_3[3], in_1[3], in_2[3]);
  xor xor_5 (out_3[4], in_1[4], in_2[4]);
  xor xor_6 (out_3[5], in_1[5], in_2[5]);
  xor xor_7 (out_3[6], in_1[6], in_2[6]);
  xor xor_8 (out_3[7], in_1[7], in_2[7]);

  // Notes on the sheet:
  //   in_1: pull=up
  //   in_2: pull=up
  //   out_3: pull=up
endmodule

module Controller (
  input  [7:0] IR,
  input  CLK,
  input  CLR,
  input  ZF,
  input  NF,
  output WC,
  output [1:0] ALU_REG,
  output [2:0] ALU_FUN,
  output ALU_RD,
  output A_WR,
  output A_RD,
  output B_WR,
  output B_RD,
  output CLC,
  output COUNT_INC,
  output IR_WR,
  output LO_WR,
  output HI_WR,
  output RAM_WR,
  output RAM_RD,
  output ROM_RD,
  output LD_COUNT,
  output IO_RD,
  output IO_WR,
  output HI_RD,
  output LO_RD,
  output F_RD,
  output F_WR,
  output HLT,
  output CTL_RST,
  output REG_ADR_WR,
  output REG_RD,
  output REG_WR,
  output SP_RAM,
  output SPH,
  output SP_WR,
  output SP_DEC,
  output SPL,
  output SP_RD
);

  wire and_1_out, and_2_out, controlled_buffer_1_out, JGT, JLT, JNZ, JZ, multiplexer_1_out,
       multiplexer_2_out, not_1_out, not_2_out, not_3_out, not_4_out, or_1_out, or_2_out, or_3_out, or_4_out,
       Shift_counter_t1, Shift_counter_t3;
  wire [7:0] counter_1_q;
  wire [31:1] rom_2_data;

  Multiplexer #(.enable("false")) multiplexer_1 (
    .in0(1'b1), .in1(1'b0), .out(multiplexer_1_out), .sel(Shift_counter_t3));
  Counter counter_1 (
    .load(Shift_counter_t3), .D(IR), .count(multiplexer_1_out), .Q(counter_1_q), .clk(not_1_out),
    .clr(Shift_counter_t1));  // open: carry
  ROM #(.dataWidth(32)) rom_1 (
    .addr(counter_1_q),
    .data({CTL_RST, HLT, JZ, JLT, JGT, JNZ, F_WR, F_RD, LO_RD, HI_RD, IO_WR, IO_RD, LD_COUNT, ROM_RD, RAM_RD, RAM_WR, HI_WR, LO_WR, IR_WR, COUNT_INC, CLC, B_RD, B_WR, A_RD, A_WR, ALU_RD, ALU_FUN, ALU_REG, WC}),
    .sel(1'b1));
  not not_1 (not_1_out, CLK);
  ROM #(.dataWidth(32)) rom_2 (
    .addr(counter_1_q),
    .data({rom_2_data[31:13], SP_RD, SPL, rom_2_data[10:9], SP_DEC, SP_WR, SPH, SP_RAM, REG_WR, REG_RD, rom_2_data[2:1], REG_ADR_WR}),
    .sel(1'b1));
  assign controlled_buffer_1_out = JNZ ? ZF : 1'bz;  // Controlled_Buffer controlled_buffer_1
  not not_2 (not_2_out, ZF);
  not not_3 (not_3_out, ZF);
  not not_4 (not_4_out, NF);
  assign controlled_buffer_1_out = JZ ? ~ZF : 1'bz;  // Controlled_Inverter controlled_inverter_1
  and and_1 (and_1_out, not_2_out, not_4_out);
  or or_1 (or_1_out, and_1_out, ZF);
  and and_2 (and_2_out, not_3_out, NF);
  Shift_counter Shift_counter (.CLK(CLK), .CLR(or_3_out), .T1(Shift_counter_t1), .T3(Shift_counter_t3));  // open: T2
  assign controlled_buffer_1_out = JLT ? or_1_out : 1'bz;  // Controlled_Buffer controlled_buffer_2
  assign controlled_buffer_1_out = JGT ? or_2_out : 1'bz;  // Controlled_Buffer controlled_buffer_3
  or or_2 (or_2_out, ZF, and_2_out);
  or or_3 (or_3_out, CTL_RST, multiplexer_2_out, CLR);
  Multiplexer #(.enable("false")) multiplexer_2 (
    .in0(1'b0), .in1(controlled_buffer_1_out), .out(multiplexer_2_out), .sel(or_4_out));
  or or_4 (or_4_out, JNZ, JZ, JLT, JGT);

  // Other names for the same wires on the sheet: RST = CTL_RST

  // Notes on the sheet:
  //   LO
  //   HI
  //   contents of rom_1 (hex, n*v repeats v):
  //   42000 1000 4*0 40200 1000 80000000 800 80000000 40000 1000 40000 1000 80000000 44000 1000 48000 1000
  //   10100 80000000 40000 1000 80 80000000 0 0 40000 1000 80000000 40000 1000 80000000 44000 1000 48000
  //   1000 20080 80000000 44000 1000 48000 1000 20200 80000000 40000 1000 44000 1000 48000 1000 20000
  //   80000000 40000 1000 200 80000000 0 0 e4 80000000 40080 1000 80000000 f0 80000000 f8 80000000 0 0 300
  //   80000000 44000 1000 48000 1000 10400 80000000 40000 1000 44000 1000 48000 1000 10000 80000000 10100
  //   0 80000000 10400 0 80000000 410000 0 80000000 810000 0 80000000 10000 0 80000000 0 8100 80000000
  //   10000 0 80000000 1010000 0 80000000 4100 80000000 40000 11000 0 80000000 0 40000000 0 480 80000000
  //   6*0 e0 80000000 6*0 e1 80000000 6*0 e8 80000000 6*0 e9 80000000 6*0 c8 80000000 40000 1000 44000
  //   1000 48000 1000 20000 10000 0 80000000 4*0 d0 80000000 17*0 44000 1000 48000 80000 80000000 0 0
  //   44000 1000 48000 1000 20000000 80000 80000000 0 0 44000 200100 1000 80000000 44000 100080 1000
  //   80000000 6*0 44000 1000 48000 1000 10000000 80000 80000000 44000 1000 48000 1000 8000000 80000
  //   80000000 0 44000 1000 48000 1000 4000000 80000 80000000
  //   contents of rom_2 (hex, n*v repeats v):
  //   11*0 1 0 10 8*0 1 0 8 0 0 0 c0 0 0 880 14*0 1 5*0 10 0 1 0 8 22*0 1 5*0 8 0 20 100 0 20 100 0 20 100
  //   0 20 100 0 1060 100 4*0 1820 100 0 20 100 0 0 0 1 28 100 46*0 1 5*0 10 28 100
endmodule

module Shift_counter_BAK (
  input  CLK,
  input  CLR,
  output T1,
  output T2,
  output T3,
  output T4
);

  wire d_ff_4_qn, d_ff_5_q;

  D_Flip_Flop d_ff_1 (.clk(CLK), .D(d_ff_5_q), .Q(T1), .preset(CLR), .en(1'b1));  // open: Qn, reset
  D_Flip_Flop d_ff_2 (.clk(CLK), .D(T1), .Q(T2), .en(1'b1), .reset(CLR));  // open: Qn, preset
  D_Flip_Flop d_ff_3 (.clk(CLK), .D(T2), .Q(T3), .en(1'b1), .reset(CLR));  // open: Qn, preset
  D_Flip_Flop d_ff_4 (.clk(CLK), .D(T3), .Q(T4), .Qn(d_ff_4_qn), .en(1'b1), .reset(CLR));  // open: preset
  D_Flip_Flop d_ff_5 (.D(T4), .Q(d_ff_5_q), .reset(CLR));  // open: clk, Qn, preset, en
endmodule

module Mainboard (
  input  MAN_CLK,
  input  MAN_AUTO,
  input  DEBUG,
  input  RESET
);

  wire and_1_out, button_2_out, button_3_out, button_out, CE_out, CLK, CTL_RST, microprocessor_1_hlt,
       microprocessor_1_io_rd, microprocessor_1_io_wr, microprocessor_1_ram_rd, microprocessor_1_ram_wr,
       microprocessor_1_rom_rd, multiplexer_1_out, multiplexer_2_out, or_1_out, s_r_ff_1_q, X_out;
  wire [7:0] controlled_buffer_1_out, controlled_buffer_2_out, controlled_buffer_4_out, D_IN2, IN0, IN1, IN2,
       IN3, IN4, IN5, IN6, IN7, microprocessor_1_mem_out, OUT0, OUT1, OUT2, OUT3, OUT4, OUT5, OUT6, OUT7,
       pio_1_bus_out, ram_1_data, rom_1_data;
  wire [15:0] microprocessor_1_adr_ram, microprocessor_1_adr_rom;

  LED led_1 (.in(OUT0[6]));
  LED led_2 (.in(OUT0[7]));
  LED led_3 (.in(OUT3[6]));
  LED led_4 (.in(OUT3[7]));
  Multiplexer #(.enable("false")) multiplexer_1 (.in0(MAN_CLK), .in1(CLK), .out(multiplexer_1_out), .sel(MAN_AUTO));
  Clock CLOCK (.out(CLK));
  Register register_1 (.Q(IN0), .clk(CLK));  // open: D, en, clr
  Register register_2 (.Q(IN4), .clk(CLK));  // open: D, en, clr
  LED led_5 (.in(OUT0[4]));
  LED led_6 (.in(OUT0[2]));
  LED led_7 (.in(OUT0[5]));
  LED led_8 (.in(OUT0[3]));
  LED led_9 (.in(OUT3[3]));
  LED led_10 (.in(OUT3[5]));
  LED led_11 (.in(OUT3[2]));
  LED led_12 (.in(OUT3[4]));
  and and_1 (and_1_out, CTL_RST, DEBUG);
  Register register_3 (.Q(IN1), .clk(CLK));  // open: D, en, clr
  Register register_4 (.Q(IN5), .clk(CLK));  // open: D, en, clr
  LED led_13 (.in(OUT0[1]));
  LED led_14 (.in(OUT0[0]));
  Hex_Digit_Display hex_digit_display_1 (.value(OUT0[7:4]));  // open: dp
  LED led_15 (.in(OUT3[0]));
  LED led_16 (.in(OUT3[1]));
  Hex_Digit_Display hex_digit_display_2 (.value(OUT3[7:4]));  // open: dp
  RAM #(.addrWidth(16), .bus("separate")) ram_1 (
    .addr(microprocessor_1_adr_ram), .din(controlled_buffer_1_out), .data(ram_1_data),
    .str(microprocessor_1_ram_wr), .sel(1'b1), .clk(multiplexer_2_out), .ld(microprocessor_1_ram_rd));  // open: clr
  ROM #(.addrWidth(16)) rom_1 (.addr(microprocessor_1_adr_rom), .data(rom_1_data), .sel(1'b1));
  Multiplexer #(.enable("false")) multiplexer_2 (
    .in0(multiplexer_1_out), .in1(1'b0), .out(multiplexer_2_out), .sel(or_1_out));
  or or_1 (or_1_out, microprocessor_1_hlt, s_r_ff_1_q);
  S_R_Flip_Flop s_r_ff_1 (.Q(s_r_ff_1_q), .preset(and_1_out), .reset(RESET));  // open: S, clk, R, Qn, en
  Hex_Digit_Display hex_digit_display_3 (.value(OUT0[3:0]));  // open: dp
  Hex_Digit_Display hex_digit_display_4 (.value(OUT3[3:0]));  // open: dp
  assign controlled_buffer_1_out = microprocessor_1_ram_wr ? microprocessor_1_mem_out : 8'bz;  // Controlled_Buffer controlled_buffer_1
  assign controlled_buffer_2_out = microprocessor_1_ram_rd ? ram_1_data : 8'bz;  // Controlled_Buffer controlled_buffer_2
  assign controlled_buffer_2_out = microprocessor_1_rom_rd ? rom_1_data : 8'bz;  // Controlled_Buffer controlled_buffer_3
  Register register_5 (.D(D_IN2), .en(1'b1), .Q(IN2), .clk(CLK));  // open: clr
  Register register_6 (.Q(IN6), .clk(CLK));  // open: D, en, clr
  LED led_17 (.in(OUT1[7]));
  LED led_18 (.in(OUT1[6]));
  LED led_19 (.in(OUT1[5]));
  LED led_20 (.in(OUT4[5]));
  LED led_21 (.in(OUT4[6]));
  LED led_22 (.in(OUT4[7]));
  Microprocessor microprocessor_1 (
    .CLK(multiplexer_2_out), .CLR(RESET), .ADR_RAM(microprocessor_1_adr_ram),
    .RAM_WR(microprocessor_1_ram_wr), .RAM_RD(microprocessor_1_ram_rd), .ROM_RD(microprocessor_1_rom_rd),
    .MEM_OUT(microprocessor_1_mem_out), .MEM_IN(controlled_buffer_2_out), .HLT(microprocessor_1_hlt),
    .IO_RD(microprocessor_1_io_rd), .IO_WR(microprocessor_1_io_wr), .ADR_ROM(microprocessor_1_adr_rom),
    .CTL_RST(CTL_RST));
  LED led_23 (.in(OUT1[3]));
  LED led_24 (.in(OUT1[4]));
  LED led_25 (.in(OUT1[1]));
  LED led_26 (.in(OUT1[2]));
  LED led_27 (.in(OUT4[2]));
  LED led_28 (.in(OUT4[3]));
  LED led_29 (.in(OUT4[1]));
  LED led_30 (.in(OUT4[4]));
  assign controlled_buffer_4_out = microprocessor_1_io_wr ? microprocessor_1_mem_out : 8'bz;  // Controlled_Buffer controlled_buffer_4
  assign controlled_buffer_2_out = microprocessor_1_io_rd ? pio_1_bus_out : 8'bz;  // Controlled_Buffer controlled_buffer_5
  Register register_7 (.Q(IN3), .clk(CLK));  // open: D, en, clr
  Register register_8 (.Q(IN7), .clk(CLK));  // open: D, en, clr
  LED led_31 (.in(OUT1[0]));
  Hex_Digit_Display hex_digit_display_5 (.value(OUT1[7:4]));  // open: dp
  LED led_32 (.in(OUT4[0]));
  Hex_Digit_Display hex_digit_display_6 (.value(OUT4[7:4]));  // open: dp
  LED led_33 (.in(D_IN2[0]));
  LED led_34 (.in(D_IN2[2]));
  Hex_Digit_Display hex_digit_display_7 (.value(OUT1[3:0]));  // open: dp
  Hex_Digit_Display hex_digit_display_8 (.value(OUT4[3:0]));  // open: dp
  LED led_35 (.in(D_IN2[1]));
  Button button (.out(button_out));
  Button X (.out(X_out));
  LED led_36 (.in(D_IN2[3]));
  LED led_37 (.in(OUT2[7]));
  LED led_38 (.in(OUT2[4]));
  LED led_39 (.in(OUT2[6]));
  LED led_40 (.in(OUT2[5]));
  LED led_41 (.in(OUT5[4]));
  LED led_42 (.in(OUT5[7]));
  LED led_43 (.in(OUT5[5]));
  LED led_44 (.in(OUT5[6]));
  PIO pio_1 (
    .IN0(IN0), .IN1(IN1), .BUS_IN(controlled_buffer_4_out), .IN2(IN2), .IN3(IN3), .IN4(IN4), .IN5(IN5),
    .IN6(IN6), .IN7(IN7), .ADDR(microprocessor_1_adr_ram), .OUT0(OUT0), .OUT1(OUT1), .BUS_OUT(pio_1_bus_out),
    .OUT2(OUT2), .OUT3(OUT3), .OUT4(OUT4), .OUT5(OUT5), .OUT6(OUT6), .OUT7(OUT7), .CLK(multiplexer_2_out),
    .WR(microprocessor_1_io_wr), .RD(microprocessor_1_io_rd), .RST(RESET));
  Button button_2 (.out(button_2_out));
  Button button_3 (.out(button_3_out));
  Button CE (.out(CE_out));
  LED led_45 (.in(OUT2[1]));
  LED led_46 (.in(OUT2[3]));
  LED led_47 (.in(OUT2[2]));
  LED led_48 (.in(OUT2[0]));
  LED led_49 (.in(OUT5[0]));
  LED led_50 (.in(OUT5[3]));
  LED led_51 (.in(OUT5[2]));
  LED led_52 (.in(OUT5[1]));
  clavier_operations OPERATION (
    .in_1(button_out), .in_2(button_2_out), .X(X_out), .in_4(button_3_out), .CE(CE_out), .out_6(D_IN2));
  Hex_Digit_Display hex_digit_display_9 (.value(OUT2[3:0]));  // open: dp
  Hex_Digit_Display hex_digit_display_10 (.value(OUT2[7:4]));  // open: dp
  Hex_Digit_Display hex_digit_display_11 (.value(OUT5[3:0]));  // open: dp
  Hex_Digit_Display hex_digit_display_12 (.value(OUT5[7:4]));  // open: dp

  // Notes on the sheet:
  //   RAM
  //   ROM
  //   contents of rom_1 (hex, n*v repeats v):
  //   3e 0 d7 1 47 d7 0 80 d3 0 d7 1 47 d7 0 90 d3 1 d7 1 47 d7 0 41 d3 2 d7 1 47 d7 0 43 d3 3 c3 2 0 76
  //   uprocessor
  //   PIO
endmodule

module Shift_counter (
  input  CLK,
  input  CLR,
  output T1,
  output T2,
  output T3
);

  wire d_ff_4_q;

  D_Flip_Flop d_ff_1 (.clk(CLK), .D(d_ff_4_q), .Q(T1), .preset(CLR), .en(1'b1));  // open: Qn, reset
  D_Flip_Flop d_ff_2 (.clk(CLK), .D(T1), .Q(T2), .en(1'b1), .reset(CLR));  // open: Qn, preset
  D_Flip_Flop d_ff_3 (.clk(CLK), .D(T2), .Q(T3), .en(1'b1), .reset(CLR));  // open: Qn, preset
  D_Flip_Flop d_ff_4 (.Q(d_ff_4_q), .reset(CLR));  // open: clk, D, Qn, preset, en
endmodule

module Microprocessor (
  input  [7:0] MEM_IN,
  input  CLK,
  input  CLR,
  output [15:0] ADR_RAM,
  output [7:0] MEM_OUT,
  output RAM_WR,
  output RAM_RD,
  output ROM_RD,
  output IO_RD,
  output IO_WR,
  output HLT,
  output CTL_RST,
  output [15:0] ADR_ROM
);

  wire ALU_cy_out, and_1_out, and_2_out, CF, Controller_a_rd, Controller_a_wr, Controller_alu_rd,
       Controller_b_rd, Controller_b_wr, Controller_clc, Controller_wc, COUNT_INC, F_RD, F_WR, HI_RD, HI_WR,
       IR_WR, LD_COUNT, LO_RD, LO_WR, NF, not_1_out, REG_ADR_WR, REG_RD, REG_WR, SP_DEC, SP_RAM, SP_RD,
       SP_WR, SPH, SPL, ZF;
  wire [1:0] Controller_alu_reg;
  wire [2:0] FN;
  wire [7:0] A_q, ALU_out, B_q, controlled_buffer_10_out, Flags_f_out, HI_q, IR, LO_q, REG_ADR_q,
       REGS_data_out, sp_1_sp_out, sp_1_sp_out_2;

  SP sp_1 (
    .SP_IN(MEM_IN), .CLK(SPH), .DEC_SP(SPL), .DEC_INC(SP_WR), .DEC_SP_2(CLK), .INC_SP(SP_DEC),
    .SP_OUT({sp_1_sp_out_2, sp_1_sp_out}));  // open: SPH, SPL, SP_WR
  Register LO (.D(MEM_IN), .en(LO_WR), .Q(LO_q), .clk(CLK), .clr(CLR));
  Register HI (.D(MEM_IN), .en(HI_WR), .Q(HI_q), .clk(CLK), .clr(CLR));
  assign MEM_IN = LO_RD ? LO_q : 8'bz;  // Controlled_Buffer controlled_buffer_1
  assign MEM_IN = HI_RD ? HI_q : 8'bz;  // Controlled_Buffer controlled_buffer_2
  assign ADR_RAM = SP_RAM ? {sp_1_sp_out_2, sp_1_sp_out} : 16'bz;  // Controlled_Buffer controlled_buffer_3
  not not_1 (not_1_out, SP_RAM);
  Counter #(.width(16), .max('hffff)) PC (
    .load(LD_COUNT), .D(ADR_RAM), .count(COUNT_INC), .Q(ADR_ROM), .clk(CLK), .clr(CLR));  // open: carry
  assign ADR_RAM = not_1_out ? {HI_q, LO_q} : 16'bz;  // Controlled_Buffer controlled_buffer_4
  assign MEM_IN = and_1_out ? sp_1_sp_out : 8'bz;  // Controlled_Buffer controlled_buffer_5
  assign MEM_IN = and_2_out ? sp_1_sp_out_2 : 8'bz;  // Controlled_Buffer controlled_buffer_6
  and and_1 (and_1_out, SP_RD, SPL);
  and and_2 (and_2_out, SP_RD, SPH);
  Register u_IR (.D(MEM_IN), .en(IR_WR), .Q(IR), .clk(CLK), .clr(CLR));
  assign MEM_IN = Controller_alu_rd ? ALU_out : 8'bz;  // Controlled_Buffer controlled_buffer_7
  assign MEM_IN = Controller_a_rd ? A_q : 8'bz;  // Controlled_Buffer controlled_buffer_8
  assign MEM_IN = Controller_b_rd ? B_q : 8'bz;  // Controlled_Buffer controlled_buffer_9
  assign controlled_buffer_10_out = REG_WR ? MEM_IN : 8'bz;  // Controlled_Buffer controlled_buffer_10
  Register A (.D(MEM_IN), .en(Controller_a_wr), .Q(A_q), .clk(CLK), .clr(CLR));
  Register B (.D(MEM_IN), .en(Controller_b_wr), .Q(B_q), .clk(CLK), .clr(CLR));
  assign MEM_IN = REG_RD ? REGS_data_out : 8'bz;  // Controlled_Buffer controlled_buffer_11
  Regs REGS (
    .DATA_IN(controlled_buffer_10_out), .WR(REG_WR), .RD(REG_RD), .CLK(CLK), .DATA_OUT(REGS_data_out),
    .REG(REG_ADR_q));
  Register REG_ADR (.D(MEM_IN), .en(REG_ADR_WR), .Q(REG_ADR_q), .clk(CLK));  // open: clr
  ALU ALU (
    .A(A_q), .B(B_q), .WC(Controller_wc), .OUT(ALU_out), .CF(CF), .REG(Controller_alu_reg), .FN(FN),
    .CY_OUT(ALU_cy_out));
  Controller Controller (
    .WC(Controller_wc), .ALU_REG(Controller_alu_reg), .ALU_FUN(FN), .IR(IR), .ALU_RD(Controller_alu_rd),
    .A_WR(Controller_a_wr), .A_RD(Controller_a_rd), .B_WR(Controller_b_wr), .B_RD(Controller_b_rd),
    .COUNT_INC(COUNT_INC), .IR_WR(IR_WR), .LO_WR(LO_WR), .HI_WR(HI_WR), .RAM_WR(RAM_WR), .RAM_RD(RAM_RD),
    .ROM_RD(ROM_RD), .LD_COUNT(LD_COUNT), .IO_RD(IO_RD), .IO_WR(IO_WR), .CLR(CLR), .CLK(CLK), .ZF(ZF),
    .HLT(HLT), .CLC(Controller_clc), .NF(NF), .REG_RD(REG_RD), .REG_WR(REG_WR), .REG_ADR_WR(REG_ADR_WR),
    .SP_RAM(SP_RAM), .SPH(SPH), .SP_WR(SP_WR), .SP_DEC(SP_DEC), .CTL_RST(CTL_RST), .HI_RD(HI_RD),
    .LO_RD(LO_RD), .F_RD(F_RD), .F_WR(F_WR), .SPL(SPL), .SP_RD(SP_RD));
  Flags Flags (
    .F_IN(MEM_IN), .ALU_OUT(ALU_out), .F_WR(F_WR), .CF_ALU(ALU_cy_out), .FN(FN), .CLK(CLK),
    .CLC(Controller_clc), .CLR(CLR), .ZF(ZF), .F_OUT(Flags_f_out), .CF(CF), .NF(NF));
  assign MEM_IN = F_RD ? Flags_f_out : 8'bz;  // Controlled_Buffer controlled_buffer_12

  assign MEM_OUT = MEM_IN;
endmodule

module PIO (
  input  [7:0] IN0,
  input  [7:0] BUS_IN,
  input  [7:0] IN1,
  input  [7:0] IN2,
  input  [7:0] IN3,
  input  [7:0] IN4,
  input  [7:0] IN5,
  input  [7:0] IN6,
  input  [7:0] IN7,
  input  CLK,
  input  RST,
  input  [15:0] ADDR,
  input  RD,
  input  WR,
  output [7:0] OUT0,
  output [7:0] OUT1,
  output [7:0] BUS_OUT,
  output [7:0] OUT2,
  output [7:0] OUT3,
  output [7:0] OUT4,
  output [7:0] OUT5,
  output [7:0] OUT6,
  output [7:0] OUT7
);

  wire demultiplexer_2_out0, demultiplexer_2_out1, demultiplexer_2_out2, demultiplexer_2_out3,
       demultiplexer_2_out4, demultiplexer_2_out5, demultiplexer_2_out6, demultiplexer_2_out7, OUT0_t,
       OUT1_t, OUT2_t, OUT3_t, OUT4_t, OUT5_t, OUT6_t, OUT7_t;
  wire [7:0] demultiplexer_1_out0, demultiplexer_1_out1, demultiplexer_1_out2, demultiplexer_1_out3,
       demultiplexer_1_out4, demultiplexer_1_out5, demultiplexer_1_out6, demultiplexer_1_out7,
       multiplexer_1_out, register_1_q, register_2_q, register_3_q, register_4_q, register_5_q, register_6_q,
       register_7_q, register_8_q;

  Register register_1 (.D(IN0), .en(1'b1), .Q(register_1_q), .clk(CLK), .clr(RST));
  Register register_2 (.D(IN1), .en(1'b1), .Q(register_2_q), .clk(CLK), .clr(RST));
  Register register_3 (.D(IN2), .en(1'b1), .Q(register_3_q), .clk(CLK), .clr(RST));
  Register register_4 (.D(IN3), .en(1'b1), .Q(register_4_q), .clk(CLK), .clr(RST));
  Register register_5 (.D(IN4), .en(1'b1), .Q(register_5_q), .clk(CLK), .clr(RST));
  Register register_6 (.D(IN5), .en(1'b1), .Q(register_6_q), .clk(CLK), .clr(RST));
  Register register_7 (.D(IN6), .en(1'b1), .Q(register_7_q), .clk(CLK), .clr(RST));
  Register register_8 (.D(IN7), .en(1'b1), .Q(register_8_q), .clk(CLK), .clr(RST));
  Multiplexer #(.select(3), .width(8), .enable("false")) multiplexer_1 (
    .in0(register_1_q), .in1(register_2_q), .in2(register_3_q), .in3(register_4_q), .in4(register_5_q),
    .in5(register_6_q), .in6(register_7_q), .in7(register_8_q), .out(multiplexer_1_out), .sel(ADDR[2:0]));
  assign BUS_OUT = RD ? multiplexer_1_out : 8'bz;  // Controlled_Buffer controlled_buffer_1
  Demultiplexer #(.select(3), .width(8)) demultiplexer_1 (
    .out0(demultiplexer_1_out0), .out1(demultiplexer_1_out1), .out2(demultiplexer_1_out2),
    .out3(demultiplexer_1_out3), .out4(demultiplexer_1_out4), .out5(demultiplexer_1_out5),
    .out6(demultiplexer_1_out6), .out7(demultiplexer_1_out7), .in(BUS_IN), .sel(ADDR[2:0]));  // open: en
  Demultiplexer #(.select(3)) demultiplexer_2 (
    .out0(demultiplexer_2_out0), .out1(demultiplexer_2_out1), .out2(demultiplexer_2_out2),
    .out3(demultiplexer_2_out3), .out4(demultiplexer_2_out4), .out5(demultiplexer_2_out5),
    .out6(demultiplexer_2_out6), .out7(demultiplexer_2_out7), .in(1'b1), .sel(ADDR[2:0]));  // open: en
  Register register_9 (.D(demultiplexer_1_out0), .en(OUT0_t), .Q(OUT0), .clk(CLK), .clr(RST));
  Register register_10 (.D(demultiplexer_1_out1), .en(OUT1_t), .Q(OUT1), .clk(CLK), .clr(RST));
  Register register_11 (.D(demultiplexer_1_out2), .en(OUT2_t), .Q(OUT2), .clk(CLK), .clr(RST));
  Register register_12 (.D(demultiplexer_1_out3), .en(OUT3_t), .Q(OUT3), .clk(CLK), .clr(RST));
  Register register_13 (.D(demultiplexer_1_out4), .en(OUT4_t), .Q(OUT4), .clk(CLK), .clr(RST));
  Register register_14 (.D(demultiplexer_1_out5), .en(OUT5_t), .Q(OUT5), .clk(CLK), .clr(RST));
  Register register_15 (.D(demultiplexer_1_out6), .en(OUT6_t), .Q(OUT6), .clk(CLK), .clr(RST));
  Register register_16 (.D(demultiplexer_1_out7), .en(OUT7_t), .Q(OUT7), .clk(CLK), .clr(RST));
  and and_1 (OUT0_t, demultiplexer_2_out0, WR);
  and and_2 (OUT1_t, demultiplexer_2_out1, WR);
  and and_3 (OUT2_t, demultiplexer_2_out2, WR);
  and and_4 (OUT3_t, demultiplexer_2_out3, WR);
  and and_5 (OUT4_t, demultiplexer_2_out4, WR);
  and and_6 (OUT5_t, demultiplexer_2_out5, WR);
  and and_7 (OUT6_t, demultiplexer_2_out6, WR);
  and and_8 (OUT7_t, demultiplexer_2_out7, WR);

  // Other names for the same wires on the sheet: ADR3[2:0] = ADDR[2:0]

  // Notes on the sheet:
  //   OUT4: pull=up
  //   OUT3: pull=up
  //   OUT5: pull=up
  //   RST: pull=up
  //   OUT7: pull=up
  //   IN7: pull=up
  //   BUS_OUT: pull=up
  //   CLK: pull=up
  //   OUT6: pull=up
  //   BUS_IN: pull=up
  //   IN5: pull=up
  //   IN1: pull=up
  //   IN4: pull=up
  //   ADDR: pull=up
  //   OUT2: pull=up
  //   OUT1: pull=up
  //   IN2: pull=up
  //   IN0: pull=up
  //   OUT0: pull=up
  //   RD: pull=up
  //   IN6: pull=up
  //   IN3: pull=up
  //   WR: pull=up
endmodule

module SP (
  input  SP_WR,
  input  SPH,
  input  SPL,
  input  CLK,
  input  DEC_SP,
  input  DEC_SP_2,
  input  INC_SP,
  input  [7:0] SP_IN,
  input  DEC_INC,
  output [15:0] SP_OUT
);

  wire adder_2_cout, and_1_out, and_2_out, not_1_out, not_2_out, subtractor_2_bout;
  wire [7:0] adder_1_out, adder_2_out, controlled_buffer_1_out, controlled_buffer_3_out, SPH_INC_DEC,
       SPL_INC_DEC, subtractor_1_out, subtractor_2_out;

  not not_1 (not_1_out, and_1_out);
  and and_1 (and_1_out, SP_WR, SPH);
  assign controlled_buffer_1_out = not_1_out ? SPH_INC_DEC : 8'bz;  // Controlled_Buffer controlled_buffer_1
  Register u_SPH (.D(controlled_buffer_1_out), .Q(SP_OUT[15:8]), .clk(CLK));  // open: en, clr
  assign controlled_buffer_1_out = and_1_out ? SP_IN : 8'bz;  // Controlled_Buffer controlled_buffer_2
  assign controlled_buffer_3_out = not_2_out ? SPL_INC_DEC : 8'bz;  // Controlled_Buffer controlled_buffer_3
  assign controlled_buffer_3_out = and_2_out ? SP_IN : 8'bz;  // Controlled_Buffer controlled_buffer_4
  Register u_SPL (.D(controlled_buffer_3_out), .Q(SP_OUT[7:0]), .clk(CLK));  // open: en, clr
  not not_2 (not_2_out, and_2_out);
  and and_2 (and_2_out, SP_WR, SPL);
  Subtractor subtractor_1 (
    .a(SP_OUT[15:8]), .b({8{1'b0}}), .out(subtractor_1_out), .bin(subtractor_2_bout));  // open: bout
  assign SPH_INC_DEC = DEC_SP ? subtractor_1_out : 8'bz;  // Controlled_Buffer controlled_buffer_5
  assign SPH_INC_DEC = DEC_INC ? adder_1_out : 8'bz;  // Controlled_Buffer controlled_buffer_6
  Adder adder_1 (.a(SP_OUT[15:8]), .b({8{1'b0}}), .out(adder_1_out), .cin(adder_2_cout));  // open: cout
  Subtractor subtractor_2 (.a(SP_OUT[7:0]), .b(8'h1), .out(subtractor_2_out), .bout(subtractor_2_bout));  // open: bin
  Adder adder_2 (.a(SP_OUT[7:0]), .b(8'h1), .out(adder_2_out), .cout(adder_2_cout));  // open: cin
  assign SPL_INC_DEC = DEC_SP_2 ? subtractor_2_out : 8'bz;  // Controlled_Buffer controlled_buffer_7
  assign SPL_INC_DEC = INC_SP ? adder_2_out : 8'bz;  // Controlled_Buffer controlled_buffer_8

  // Other names for the same wires on the sheet: SPL_Q[7:0] = SP_OUT[7:0]; SPH_Q[7:0] = SP_OUT[15:8]

  // Notes on the sheet:
  //   SP_IN: pull=up
  //   SP_OUT: pull=up
endmodule

module Flags (
  input  [7:0] F_IN,
  input  [7:0] ALU_OUT,
  input  F_WR,
  input  CF_ALU,
  input  [2:0] FN,
  input  CLK,
  input  CLC,
  input  CLR,
  output ZF,
  output [7:0] F_OUT,
  output CF,
  output NF
);

  wire ALU_Z, and_1_out, and_2_out, CF_D, NF_D, not_1_out, not_2_out, not_3_out, not_4_out, or_1_out,
       or_2_out, or_3_out, or_4_out, or_5_out, or_6_out, or_7_out, ZF_D;

  or or_1 (or_1_out, FN[0], FN[1], FN[2]);
  not not_1 (not_1_out, FN[1]);
  not not_2 (not_2_out, FN[2]);
  not not_3 (not_3_out, FN[1]);
  assign ZF_D = not_4_out ? ALU_Z : 1'bz;  // Controlled_Buffer controlled_buffer_1
  not not_4 (not_4_out, F_WR);
  and and_1 (and_1_out, FN[0], not_1_out, not_2_out);
  and and_2 (and_2_out, FN[0], not_3_out, FN[2]);
  assign ZF_D = F_WR ? F_IN[0] : 1'bz;  // Controlled_Buffer controlled_buffer_2
  or or_2 (or_2_out, ALU_OUT[0], ALU_OUT[1], ALU_OUT[2], ALU_OUT[3], ALU_OUT[4], ALU_OUT[5], ALU_OUT[6], ALU_OUT[7]);
  not not_5 (ALU_Z, or_2_out);
  or or_3 (or_3_out, and_1_out, and_2_out);
  or or_4 (or_4_out, or_1_out, F_WR);
  or or_5 (or_5_out, or_3_out, F_WR);
  or or_6 (or_6_out, or_1_out, F_WR);
  Register #(.width(1)) u_ZF (.D(ZF_D), .en(or_4_out), .Q(F_OUT[0]), .clk(CLK), .clr(CLR));
  Register #(.width(1)) u_CF (.D(CF_D), .en(or_5_out), .Q(CF), .clk(CLK), .clr(or_7_out));
  or or_7 (or_7_out, CLC, CLR);
  Register #(.width(1)) u_NF (.D(NF_D), .en(or_6_out), .Q(F_OUT[2]), .clk(CLK), .clr(CLR));

  assign {F_OUT[7:3], F_OUT[1]} = {{5{1'b0}}, CF};
  assign NF = F_OUT[2];
  assign ZF = F_OUT[0];

  // Other names for the same wires on the sheet: ALU_CF = CF_ALU; ALU_N = ALU_OUT[7]; ZF_IN = F_IN[0];
  //   CF_IN = F_IN[1]; NF_IN = F_IN[2]

  // Notes on the sheet:
  //   F_IN: pull=up
  //   F_OUT: pull=up
  //   F_WR: pull=up
  //   CF: pull=up
  //   FN: pull=up
  //   CLC: pull=up
  //   ZF: pull=up
  //   CF_ALU: pull=up
  //   NF: pull=up
  //   ALU_OUT: pull=up
  //   CLR: pull=up
  //   CLK: pull=up
  //   FN ADD
  //   FN SUB
  //   FN
  //   000 - nop
  //   001 - AND
  //   010 - OR
  //   011 - XOR
  //   100 - ADD
  //   101 - SUB
  //   110 - not used
  //   111 - not used
endmodule

module Regs (
  input  [7:0] DATA_IN,
  input  WR,
  input  [7:0] REG,
  input  RD,
  input  CLK,
  output [7:0] DATA_OUT
);

  wire and_1_out, and_2_out, and_3_out, and_4_out, and_5_out, and_6_out, and_7_out, and_8_out,
       demultiplexer_1_out0, demultiplexer_1_out1, demultiplexer_1_out2, demultiplexer_1_out3,
       demultiplexer_1_out4, demultiplexer_1_out5, demultiplexer_1_out6, demultiplexer_1_out7;
  wire [7:0] controlled_buffer_1_out, multiplexer_1_out, register_1_q, register_2_q, register_3_q,
       register_4_q, register_5_q, register_6_q, register_7_q, register_8_q;

  Demultiplexer #(.select(3)) demultiplexer_1 (
    .out0(demultiplexer_1_out0), .out1(demultiplexer_1_out1), .out2(demultiplexer_1_out2),
    .out3(demultiplexer_1_out3), .out4(demultiplexer_1_out4), .out5(demultiplexer_1_out5),
    .out6(demultiplexer_1_out6), .out7(demultiplexer_1_out7), .in(1'b1), .sel(REG[2:0]));  // open: en
  and and_1 (and_1_out, WR, demultiplexer_1_out0);
  and and_2 (and_2_out, WR, demultiplexer_1_out1);
  and and_3 (and_3_out, WR, demultiplexer_1_out2);
  and and_4 (and_4_out, WR, demultiplexer_1_out3);
  and and_5 (and_5_out, WR, demultiplexer_1_out4);
  and and_6 (and_6_out, WR, demultiplexer_1_out5);
  and and_7 (and_7_out, WR, demultiplexer_1_out6);
  and and_8 (and_8_out, WR, demultiplexer_1_out7);
  assign controlled_buffer_1_out = WR ? DATA_IN : 8'bz;  // Controlled_Buffer controlled_buffer_1
  Register register_1 (.D(controlled_buffer_1_out), .en(and_1_out), .Q(register_1_q), .clk(CLK));  // open: clr
  Register register_2 (.D(controlled_buffer_1_out), .en(and_2_out), .Q(register_2_q), .clk(CLK));  // open: clr
  Register register_3 (.D(controlled_buffer_1_out), .en(and_3_out), .Q(register_3_q), .clk(CLK));  // open: clr
  Register register_4 (.D(controlled_buffer_1_out), .en(and_4_out), .Q(register_4_q), .clk(CLK));  // open: clr
  Register register_5 (.D(controlled_buffer_1_out), .en(and_5_out), .Q(register_5_q), .clk(CLK));  // open: clr
  Register register_6 (.D(controlled_buffer_1_out), .en(and_6_out), .Q(register_6_q), .clk(CLK));  // open: clr
  Register register_7 (.D(controlled_buffer_1_out), .en(and_7_out), .Q(register_7_q), .clk(CLK));  // open: clr
  Register register_8 (.D(controlled_buffer_1_out), .en(and_8_out), .Q(register_8_q), .clk(CLK));  // open: clr
  Multiplexer #(.select(3), .width(8), .enable("false")) multiplexer_1 (
    .in0(register_1_q), .in1(register_2_q), .in2(register_3_q), .in3(register_4_q), .in4(register_5_q),
    .in5(register_6_q), .in6(register_7_q), .in7(register_8_q), .out(multiplexer_1_out), .sel(REG[2:0]));
  assign DATA_OUT = RD ? multiplexer_1_out : 8'bz;  // Controlled_Buffer controlled_buffer_2

  // Other names for the same wires on the sheet: REG_t[2:0] = REG[2:0]

  // Notes on the sheet:
  //   WR: pull=up
  //   DATA_IN: pull=up
  //   REG: pull=up
  //   DATA_OUT: pull=up
  //   CLK: pull=up
  //   RD: pull=up
endmodule

module clavier_operations (
  input  in_1,
  input  in_2,
  input  X,
  input  in_4,
  input  CE,
  output [7:0] out_6
);

  wire or_1_out, or_2_out, or_3_out, or_4_out;
  wire [3:0] SEL;

  S_R_Flip_Flop s_r_ff_1 (.Q(SEL[0]), .preset(in_1), .reset(or_1_out));  // open: S, clk, R, Qn, en
  or or_1 (or_1_out, in_2, X, in_4, CE);
  S_R_Flip_Flop s_r_ff_2 (.Q(SEL[1]), .preset(in_2), .reset(or_2_out));  // open: S, clk, R, Qn, en
  or or_2 (or_2_out, in_1, X, in_4, CE);
  S_R_Flip_Flop s_r_ff_3 (.Q(SEL[2]), .preset(X), .reset(or_3_out));  // open: S, clk, R, Qn, en
  or or_3 (or_3_out, in_2, in_1, in_4, CE);
  S_R_Flip_Flop s_r_ff_4 (.Q(SEL[3]), .preset(in_4), .reset(or_4_out));  // open: S, clk, R, Qn, en
  or or_4 (or_4_out, in_2, X, in_1, CE);
  LED led (.in(SEL[0]));
  LED led_2 (.in(SEL[1]));
  LED u_X (.in(SEL[2]));
  LED led_3 (.in(SEL[3]));
  Multiplexer #(.select(4), .width(8), .enable("false")) multiplexer_1 (
    .in0({8{1'b0}}), .in1(8'h1), .in2(8'h2), .in3({8{1'b0}}), .in4(8'h4), .in5({8{1'b0}}), .in6({8{1'b0}}),
    .in7({8{1'b0}}), .in8(8'h8), .in9({8{1'b0}}), .in10({8{1'b0}}), .in11({8{1'b0}}), .in12({8{1'b0}}),
    .in13({8{1'b0}}), .in14({8{1'b0}}), .in15({8{1'b0}}), .out(out_6), .sel(SEL));

  // Other names for the same wires on the sheet: A = in_1; B = in_2; C = X; D = in_4; E = CE

  // Notes on the sheet:
  //   in_1: pull=up
  //   out_6: pull=up
  //   X: pull=up
  //   CE: pull=up
  //   in_4: pull=up
  //   in_2: pull=up
  //   000 - no operation
  //   0001 - ADD
  //   0010 - SUB
  //   0100 - MUL
  //   1000 - DIV
endmodule
